# Fritzing sketch Photogrammetry Turntable Schematic (saved by Fritzing 0.9.4)
breadboards: 1

parts:
  Part1 = Arduino Uno (Rev3)
  Driver1 = 28BYJ-48 Driver Module [part_number=ULN2003 package=THT]
  U1 = Optocoupler [package=THT]
  SM1 = 28BYJ-48 Stepper Motor [part_number=28BYJ-48]
  J2 = Piezo Speaker
  S1 = Pushbutton [package="[SMD]"]
  R2 = Resistor [tolerance=±5% resistance=1k package="1206 [SMD]"]
  R3 = Resistor [tolerance=±5% resistance=220 package="0805 [SMD]"]
  R4 = Resistor [tolerance=±5% resistance=220 package="2010 [SMD]"]
  J3 = Power Jack [package=power_jack_smd]

nets:
  N1: Part1.D8, Driver1.IN1
  N2: Part1.D9_PWM, Driver1.IN2
  N3: Part1.D10_PWM/SS, Driver1.IN3
  N4: Part1.D11_PWM/MOSI, Driver1.IN4
  N5: Part1.D12/MISO, S1.Pin_1, S1.Pin_2, R3.Pin_0
  N6: Part1.D13/SCK, R2.Pin_1
  N7: Part1.D7, R4.Pin_1
  N8: Part1.5V, S1.Pin_3, S1.Pin_4
  GND: Part1.GND, Driver1.GND, J2.pin1, R3.Pin_1, J3.GNDBREAK
  N9: Driver1.Vmotor, J3.GND
  N10: Driver1.blue-pin, SM1.blue-pin
  N11: Driver1.pink-pin, SM1.pink-pin
  N12: Driver1.yellow-pin, SM1.yellow-pin
  N13: Driver1.orange-pin, SM1.orange-pin
  N14: Driver1.red-pin, SM1.red-pin
  N15: U1.Pin_1, R2.Pin_0

custom parts:
  28BYJ-48 Driver Module: ULN2003 Driver Module for the 28BYJ-48 Unipolar Stepper Motor LED A - Blue wire - Bottom coil left LED B - Pink wire - Top coil left LED C - Yellow wire - Bottom coil right LED D - Orange wire - Top coil right Common rail - red Connector pins: blue - pink - yellow - orange - red Control pins - IN1 to IN4 Power pins - GND & Vmotor (5-12V) On/Off jumper (if removed, power to motor is cut).
  28BYJ-48 Stepper Motor: Unipolar Stepper Motor 28BYJ-48 Top coil - pink & orange Bottom coil - blue & yellow Common rail - red Connector pins: blue - pink - yellow - orange - red
